# Fritzing sketch DO_CONNECTION (saved by Fritzing 0.9.9b)

parts:
  RS485_Connect_Sensor = RS485_XY-017 [part_number=XY-017]
  RTC_DS3231 = ZS-042 RTC Module
  Grove1 = Grove OLED 128x96
  SDCard_Module = MicroSD Card Module
  MH-ET_LIVE_ESP32_DEVKIT1 = MH-ET LIVE ESP32 DEVKIT 38 pins

nets:
  N1: RS485_Connect_Sensor.VCC, MH-ET_LIVE_ESP32_DEVKIT1.IO4
  N2: RS485_Connect_Sensor.TXD, MH-ET_LIVE_ESP32_DEVKIT1.IO17
  N3: RS485_Connect_Sensor.RXD, MH-ET_LIVE_ESP32_DEVKIT1.IO16
  N4: RTC_DS3231.SDA, Grove1.SDA, MH-ET_LIVE_ESP32_DEVKIT1.IO21
  N5: RTC_DS3231.SCL, Grove1.SCL, MH-ET_LIVE_ESP32_DEVKIT1.IO22
  N6: SDCard_Module.MISO, MH-ET_LIVE_ESP32_DEVKIT1.IO19
  N7: SDCard_Module.MOSI, MH-ET_LIVE_ESP32_DEVKIT1.IO23
  N8: SDCard_Module.SCK, MH-ET_LIVE_ESP32_DEVKIT1.IO18
  N9: SDCard_Module.CS, MH-ET_LIVE_ESP32_DEVKIT1.IO5

notes:
  DO MEASUREMENT SYSTEM

custom parts:
  RS485_XY-017: Commercially available RS485 to RS232 TTL Module
  MH-ET LIVE ESP32 DEVKIT 38 pins: http://mh.nodebb.com/topic/2/mh-et-live-esp32-devkit
